// Logisim project MouseProject.circ as structural Verilog
module main (
  input  CLOCK,
  input  RESET,
  input  REVERSE,
  input  PCLOCK,
  input  PDATA,
  output IS_LEFT,
  output [3:0] ANODES,
  output [6:0] CATODES
);

  wire control_unit_1_dec, control_unit_1_inc, ps2_reader_1_left_click, ps2_reader_1_right_click;
  wire [15:0] counter_1_outnumber;

  PS2_READER ps2_reader_1 (
    .CLOCK(CLOCK), .RESET(RESET), .PS2_CLOCK(PCLOCK), .PS2_DATA(PDATA), .LEFT_CLICK(ps2_reader_1_left_click),
    .RIGHT_CLICK(ps2_reader_1_right_click));
  CONTROL_UNIT control_unit_1 (
    .CLOCK(CLOCK), .RESET(RESET), .REVERSE(REVERSE), .LEFT_CLICK(ps2_reader_1_left_click),
    .RIGHT_CLICK(ps2_reader_1_right_click), .IS_LEFT(IS_LEFT), .INC(control_unit_1_inc),
    .DEC(control_unit_1_dec));
  COUNTER counter_1 (
    .CLOCK(CLOCK), .RESET(RESET), .INCREMENT(control_unit_1_inc), .DECREMENT(control_unit_1_dec),
    .OUTNUMBER(counter_1_outnumber));
  SSD_MANAGER ssd_manager_1 (
    .CLOCK(CLOCK), .RESET(RESET), .NUMBER(counter_1_outnumber), .ANODES(ANODES), .CATODES(CATODES));
endmodule

// VHDL entity PS2_READER, as the project stores it:
library ieee;
use ieee.std_logic_1164.all;
use ieee.std_logic_unsigned.all;

entity PS2_READER is
	port (
		CLOCK : in std_logic;
		RESET : in std_logic;
		PS2_CLOCK : in std_logic;
		PS2_DATA : in std_logic;
		LEFT_CLICK : out std_logic;
		RIGHT_CLICK : out std_logic
	);
end PS2_READER;

architecture Behavioral of PS2_READER is
	signal MOUSE_REGISTER : std_logic_vector(42 downto 0) := (others => '0');
	signal MOUSE_BITS : std_logic_vector(5 downto 0) := (others => '0');
	signal REGISTER_FULL : std_logic;
	signal IS_LEFT_PRESSED : std_logic := '0';
	signal IS_RIGHT_PRESSED : std_logic := '0';
	signal IDLE : std_logic := '1';
 
begin
	BIT_COUNT_PROCESS : process (PS2_CLOCK, RESET)
	begin
		if RESET = '0' then
			MOUSE_BITS <= (others => '0');
		elsif falling_edge(PS2_CLOCK) then
			if MOUSE_BITS <= 42 then
				MOUSE_BITS <= MOUSE_BITS + 1;
			else
				MOUSE_BITS <= (others => '0');
			end if;
		end if;
	end process;

	REGISTER_PROCESS : process (PS2_CLOCK, RESET)
	begin
		REGISTER_FULL <= '0';
		if RESET = '0' then
			MOUSE_REGISTER <= (others => '0');
		elsif falling_edge(PS2_CLOCK) then
			MOUSE_REGISTER <= MOUSE_REGISTER(41 downto 0) & PS2_DATA;
			if MOUSE_BITS = 42 then
				REGISTER_FULL <= '1';
			end if;
		end if;
	end process;

	SIGNAL_PROCESS: process (CLOCK)
	begin
		if rising_edge(CLOCK) then
			LEFT_CLICK <= '0';
			RIGHT_CLICK <= '0';
			
			if REGISTER_FULL = '1' then
				
				if MOUSE_REGISTER(41) = '1' and IS_LEFT_PRESSED = '0' then
					LEFT_CLICK <= '1';
				elsif MOUSE_REGISTER(40) = '1' and IS_RIGHT_PRESSED = '0' then
					RIGHT_CLICK <= '1';
				end if;
				IS_LEFT_PRESSED <= MOUSE_REGISTER(41);
				IS_RIGHT_PRESSED <= MOUSE_REGISTER(40);
			end if;	
		end if;
	end process;
--	COUNTER_PROCESS : process (CLOCK, RESET)
--	begin
--		if RESET = '0' then
--			CLICK_COUNT <= (others => '0');
--		elsif rising_edge(CLOCK) then
--			if REGISTER_FULL = '1' then
--				if MOUSE_REGISTER(41) = '1' and IS_LEFT_PRESSED = '0' then
--					CLICK_COUNT <= CLICK_COUNT + 1;
--				elsif MOUSE_REGISTER(40) = '1' and IS_RIGHT_PRESSED = '0' then
--					CLICK_COUNT <= CLICK_COUNT - 1;
--				end if;
--				IS_LEFT_PRESSED <= MOUSE_REGISTER(41);
--				IS_RIGHT_PRESSED <= MOUSE_REGISTER(40);
--			end if;
--		end if;
--
--		TEST <= CLICK_COUNT;
--	end process;
end Behavioral;

// VHDL entity COUNTER, as the project stores it:
LIBRARY ieee;
USE ieee.std_logic_1164.all;
use ieee.std_logic_unsigned.all;

ENTITY COUNTER IS
  PORT (
  	CLOCK: in std_logic;
  	RESET: in std_logic;
  	INCREMENT, DECREMENT: in std_logic;
  	OUTNUMBER: out std_logic_vector(15 downto 0)
    );
END COUNTER;



ARCHITECTURE Behavioral OF COUNTER IS
signal NUMBER: std_logic_vector(15 downto 0) := (others => '0');
BEGIN
	CLOCK_ACTIVE: process (CLOCK, RESET)
	begin
		if RESET = '0' then
			NUMBER <= (others => '0');
		elsif rising_edge(CLOCK) then
			if INCREMENT = '1' then
				if NUMBER < 9999 then
					NUMBER <= NUMBER + 1;
				else
					NUMBER <= "0010011100001111"; --9999
				end if;
			elsif DECREMENT = '1' then
				if NUMBER > 0 then
					NUMBER <= NUMBER - 1;
				else 
					NUMBER <= (others => '0');
				end if;
			end if;
		end if;
		OUTNUMBER <= NUMBER;
	end process;

END Behavioral;

// VHDL entity CONTROL_UNIT, as the project stores it:
LIBRARY ieee;
USE ieee.std_logic_1164.all;

ENTITY CONTROL_UNIT IS
  PORT (
	CLOCK: in std_logic;
	RESET: in std_logic;
	REVERSE: in std_logic;
	LEFT_CLICK, RIGHT_CLICK: in std_logic;
	IS_LEFT, INC, DEC: out std_logic
    );
END CONTROL_UNIT;


ARCHITECTURE Behavioral OF CONTROL_UNIT IS

BEGIN
	CONTROL_UNIT: process (CLOCK, RESET)
	begin
		if RESET = '0' then
			INC <= '0';
			DEC <= '0';
		elsif rising_edge(CLOCK) then
			INC <= '0';
			DEC <= '0';
			if REVERSE = '0' then
				IS_LEFT <= '1';
				if LEFT_CLICK = '1' then
					INC <= '1';
		
				elsif RIGHT_CLICK = '1' then
					DEC <= '1';
					
				end if;
			else
				IS_LEFT <= '0';
				if LEFT_CLICK = '1' then
					DEC <= '1';
					
				elsif RIGHT_CLICK = '1' then
					INC <= '1';
					
				end if;
				
			end if;
		end if;
	end process;

END Behavioral;

// VHDL entity BCD7SGT, as the project stores it:
LIBRARY ieee;
USE ieee.std_logic_1164.all;

ENTITY BCD7SGT IS
  PORT (
  	INPUT: in std_logic_vector(3 downto 0);
  	OUTPUT: out std_logic_vector(6 downto 0)
    );
END BCD7SGT;


ARCHITECTURE Behavioral OF BCD7SGT IS

BEGIN
	with INPUT select OUTPUT <=
		"1111110" when "0000",
		"0110000" when "0001",
		"1101101" when "0010",
		"1111001" when "0011",
		"0110011" when "0100",
		"1011011" when "0101",
		"1011111" when "0110",
		"1110000" when "0111",
		"1111111" when "1000",
		"1111011" when "1001",
		"1110111" when "1010",
		"0011111" when "1011",
		"1001110" when "1100",
		"0111101" when "1101",
		"1001111" when "1110",
		"1000111" when "1111",
		"0000000" when others;
END Behavioral;

// VHDL entity RING_SHIFTER, as the project stores it:
LIBRARY ieee;
USE ieee.std_logic_1164.all;
use ieee.std_logic_unsigned.all;

ENTITY RING_SHIFTER IS
  PORT (
	CLOCK: in std_logic;
	RESET: in std_logic;
	OUTPUT: out std_logic_vector(3 downto 0)
    );
END RING_SHIFTER;

ARCHITECTURE TypeArchitecture OF RING_SHIFTER IS
	signal CONTENT: std_logic_vector(3 downto 0) := "0001";
BEGIN
	CLOCK_SIGNAL: process (CLOCK, RESET)
	begin
		if RESET = '0' then
			CONTENT <= "0001";
		elsif rising_edge(CLOCK) then
			CONTENT <= CONTENT(0) & CONTENT(3 downto 1);
		end if;
		OUTPUT <= CONTENT;

	end process;

END TypeArchitecture;

// VHDL entity MUX4TO1, as the project stores it:
LIBRARY ieee;
USE ieee.std_logic_1164.all;
use ieee.std_logic_unsigned.all;

ENTITY MUX4TO1 IS
  PORT (
	INPUT1: in std_logic_vector(3 downto 0);
	INPUT2: in std_logic_vector(3 downto 0);
	INPUT3: in std_logic_vector(3 downto 0);
	INPUT4: in std_logic_vector(3 downto 0);
	SELECTION: in std_logic_vector(1 downto 0);
	OUTPUT: out std_logic_vector(3 downto 0)
    );
END MUX4TO1;

ARCHITECTURE Behavioral OF MUX4TO1 IS
BEGIN

	OUTPUT <= INPUT1 when SELECTION = "00" else
		INPUT2 when SELECTION = "01" else
	 	INPUT3 when SELECTION = "10" else 
	 	INPUT4 when SELECTION = "11";

END Behavioral;

// VHDL entity PRIORITY_ENCODER, as the project stores it:
LIBRARY ieee;
USE ieee.std_logic_1164.all;

ENTITY PRIORITY_ENCODER IS
  PORT (
	INPUT: in std_logic_vector(3 downto 0);
	OUTPUT: out std_logic_vector(1 downto 0)
    );
END PRIORITY_ENCODER;


ARCHITECTURE Behavioral OF PRIORITY_ENCODER IS

BEGIN

	OUTPUT <= "11" when INPUT(3) = '1' else
			"10" when INPUT(3 downto 2) = "01" else
			"01" when INPUT(3 downto 1) = "001" else
			"00" when INPUT(3 downto 0) = "0001";

END Behavioral;

// VHDL entity DIGIT_SPLITTER, as the project stores it:
LIBRARY ieee;
USE ieee.std_logic_1164.all;
use ieee.std_logic_unsigned.all;
use ieee.numeric_std.all;

ENTITY DIGIT_SPLITTER IS
  PORT (
	NUMBER: in std_logic_vector(15 downto 0);
	D1, D2, D3, D4: out std_logic_vector(3 downto 0)
    );
END DIGIT_SPLITTER;


ARCHITECTURE Behavioral OF DIGIT_SPLITTER IS

BEGIN
	SPLIT: process(NUMBER) 
	variable DECIMAL : integer := 0;
	variable N: integer := 0;
	begin
		N := conv_integer(NUMBER);
		DECIMAL := N rem 10;
		D1 <= std_logic_vector(to_unsigned(DECIMAL, 4));
		N := N / 10;
		DECIMAL := N rem 10;
		D2 <= std_logic_vector(to_unsigned(DECIMAL, 4));
		N := N / 10;
		DECIMAL := N rem 10;
		D3 <= std_logic_vector(to_unsigned(DECIMAL, 4));
		N := N / 10;
		DECIMAL := N rem 10;
		D4 <= std_logic_vector(to_unsigned(DECIMAL, 4));
	end process;

END Behavioral;

// VHDL entity FREQUENCY_DIVIDER, as the project stores it:
LIBRARY ieee;
USE ieee.std_logic_1164.all;
USE ieee.std_logic_unsigned.all;

ENTITY FREQUENCY_DIVIDER IS
  PORT (
  	CLOCK_100: in std_logic;
  	RESET: in std_logic;
  	CLK_DIVIDED: out std_logic
	);
END FREQUENCY_DIVIDER;


ARCHITECTURE Behavioral OF FREQUENCY_DIVIDER IS

BEGIN

	process(CLOCK_100)
	variable nr: std_logic_vector (15 downto 0) := (others => '0');
	begin
		if RESET = '0' then
			nr := (others => '0');
		elsif rising_edge(CLOCK_100) then
			nr := nr + 1;
		end if;
		CLK_DIVIDED <= nr(15);
	end process;

END Behavioral;

// VHDL entity SSD_MANAGER, as the project stores it:
LIBRARY ieee;
USE ieee.std_logic_1164.all;

ENTITY SSD_MANAGER IS
  PORT (
  	CLOCK: in std_logic;
  	RESET: in std_logic;
	NUMBER: in std_logic_vector(15 downto 0);
	ANODES: out std_logic_vector(3 downto 0);
	CATODES: out std_logic_vector(6 downto 0)
    );
END SSD_MANAGER;


ARCHITECTURE Structural OF SSD_MANAGER IS
	COMPONENT FREQUENCY_DIVIDER IS
	  PORT (
	  	CLOCK_100: in std_logic;
	  	RESET: in std_logic;
	  	CLK_DIVIDED: out std_logic
		);
	END component;

	component RING_SHIFTER IS
	  PORT (
		CLOCK: in std_logic;
		RESET: in std_logic;
		OUTPUT: out std_logic_vector(3 downto 0)
	    );
	END component;

	component PRIORITY_ENCODER IS
		  PORT (
			INPUT: in std_logic_vector(3 downto 0);
			OUTPUT: out std_logic_vector(1 downto 0)
		    );
	END component;

	component DIGIT_SPLITTER IS
	  PORT (
		NUMBER: in std_logic_vector(15 downto 0);
		D1, D2, D3, D4: out std_logic_vector(3 downto 0)
	    );
	END component;

	component MUX4TO1 IS
	  PORT (
		INPUT1: in std_logic_vector(3 downto 0);
		INPUT2: in std_logic_vector(3 downto 0);
		INPUT3: in std_logic_vector(3 downto 0);
		INPUT4: in std_logic_vector(3 downto 0);
		SELECTION: in std_logic_vector(1 downto 0);
		OUTPUT: out std_logic_vector(3 downto 0)
	    );
	END component;

	component BCD7SGT IS
	  PORT (
	  	INPUT: in std_logic_vector(3 downto 0);
	  	OUTPUT: out std_logic_vector(6 downto 0)
	    );
	END component;

	signal CLOCK_DIVIDED: std_logic;
	signal ANODES_SIGNAL: std_logic_vector(3 downto 0);
	signal ANODE_SELECT: std_logic_vector(1 downto 0);
	signal DIGIT_SELECT: std_logic_vector(3 downto 0);
	signal DIGIT1, DIGIT2, DIGIT3, DIGIT4: std_logic_vector(3 downto 0);

BEGIN

FREQ_DIV: FREQUENCY_DIVIDER port map(CLOCK, RESET, CLOCK_DIVIDED);
RING_SHIFT: RING_SHIFTER port map(CLOCK_DIVIDED, RESET, ANODES_SIGNAL);
ANODES <= ANODES_SIGNAL;
PRIORITY_ENC: PRIORITY_ENCODER port map(ANODES_SIGNAL, ANODE_SELECT);
DIGIT_SPLT: DIGIT_SPLITTER port map(NUMBER, DIGIT1, DIGIT2, DIGIT3, DIGIT4);
MUX: MUX4TO1 port map(DIGIT1, DIGIT2, DIGIT3, DIGIT4, ANODE_SELECT, DIGIT_SELECT);
DIGIT_DEC: BCD7SGT port map(DIGIT_SELECT, CATODES);
END Structural;


-------------------------------------------------------
------------------ FREQUENCY DIVIDER ------------------
-------------------------------------------------------

LIBRARY ieee;
USE ieee.std_logic_1164.all;
USE ieee.std_logic_unsigned.all;

ENTITY FREQUENCY_DIVIDER IS
  PORT (
  	CLOCK_100: in std_logic;
  	RESET: in std_logic;
  	CLK_DIVIDED: out std_logic
	);
END FREQUENCY_DIVIDER;


ARCHITECTURE Behavioral OF FREQUENCY_DIVIDER IS

BEGIN

	process(CLOCK_100)
	variable nr: std_logic_vector (15 downto 0) := (others => '0');
	begin
		if RESET = '0' then
			nr := (others => '0');
		elsif rising_edge(CLOCK_100) then
			nr := nr + 1;
		end if;
		--CHANGE TO 15
		CLK_DIVIDED <= nr(15);
	end process;

END Behavioral;


-------------------------------------------------------
--------------------- RING SHIFTER --------------------
-------------------------------------------------------

LIBRARY ieee;
USE ieee.std_logic_1164.all;
use ieee.std_logic_unsigned.all;

ENTITY RING_SHIFTER IS
  PORT (
	CLOCK: in std_logic;
	RESET: in std_logic;
	OUTPUT: out std_logic_vector(3 downto 0)
    );
END RING_SHIFTER;

ARCHITECTURE TypeArchitecture OF RING_SHIFTER IS
	signal CONTENT: std_logic_vector(3 downto 0) := "0001";
BEGIN

	CLOCK_SIGNAL: process (CLOCK)
	begin
		
		if RESET = '0' then
			CONTENT <= "0001";
		elsif rising_edge(CLOCK) then
			CONTENT <= CONTENT(0) & CONTENT(3 downto 1);
		end if;

		OUTPUT <= CONTENT;

	end process;

END TypeArchitecture;




-------------------------------------------------------
------------------- PROPRITY ENCODER ------------------
-------------------------------------------------------

LIBRARY ieee;
USE ieee.std_logic_1164.all;

ENTITY PRIORITY_ENCODER IS
  PORT (
	INPUT: in std_logic_vector(3 downto 0);
	OUTPUT: out std_logic_vector(1 downto 0)
    );
END PRIORITY_ENCODER;

ARCHITECTURE Behavioral OF PRIORITY_ENCODER IS

BEGIN

	OUTPUT <= "11" when INPUT(3) = '1' else
			"10" when INPUT(3 downto 2) = "01" else
			"01" when INPUT(3 downto 1) = "001" else
			"00" when INPUT(3 downto 0) = "0001";

END Behavioral;


-------------------------------------------------------
------------------- DIGIT_SPLITTER --------------------
-------------------------------------------------------

LIBRARY ieee;
USE ieee.std_logic_1164.all;
use ieee.std_logic_unsigned.all;
use ieee.numeric_std.all;

ENTITY DIGIT_SPLITTER IS
  PORT (
	NUMBER: in std_logic_vector(15 downto 0);
	D1, D2, D3, D4: out std_logic_vector(3 downto 0)
    );
END DIGIT_SPLITTER;


ARCHITECTURE Behavioral OF DIGIT_SPLITTER IS

BEGIN
	SPLIT: process(NUMBER) 
	variable DECIMAL : integer := 0;
	variable N: integer := 0;
	begin
		N := conv_integer(NUMBER);
		DECIMAL := N rem 10;
		D1 <= std_logic_vector(to_unsigned(DECIMAL, 4));
		N := N / 10;
		DECIMAL := N rem 10;
		D2 <= std_logic_vector(to_unsigned(DECIMAL, 4));
		N := N / 10;
		DECIMAL := N rem 10;
		D3 <= std_logic_vector(to_unsigned(DECIMAL, 4));
		N := N / 10;
		DECIMAL := N rem 10;
		D4 <= std_logic_vector(to_unsigned(DECIMAL, 4));
	end process;

END Behavioral;


-------------------------------------------------------
------------------ MUX 4 TO 1 4BIT --------------------
-------------------------------------------------------

LIBRARY ieee;
USE ieee.std_logic_1164.all;
use ieee.std_logic_unsigned.all;

ENTITY MUX4TO1 IS
  PORT (
	INPUT1: in std_logic_vector(3 downto 0);
	INPUT2: in std_logic_vector(3 downto 0);
	INPUT3: in std_logic_vector(3 downto 0);
	INPUT4: in std_logic_vector(3 downto 0);
	SELECTION: in std_logic_vector(1 downto 0);
	OUTPUT: out std_logic_vector(3 downto 0)
    );
END MUX4TO1;

ARCHITECTURE Behavioral OF MUX4TO1 IS
BEGIN

	OUTPUT <= INPUT1 when SELECTION = "00" else
		INPUT2 when SELECTION = "01" else
	 	INPUT3 when SELECTION = "10" else 
	 	INPUT4 when SELECTION = "11";

END Behavioral;



-------------------------------------------------------
------------------- BCD TO 7 SEGMENT ------------------
-------------------------------------------------------

LIBRARY ieee;
USE ieee.std_logic_1164.all;

ENTITY BCD7SGT IS
  PORT (
  	INPUT: in std_logic_vector(3 downto 0);
  	OUTPUT: out std_logic_vector(6 downto 0)
    );
END BCD7SGT;


ARCHITECTURE Behavioral OF BCD7SGT IS

BEGIN
	with INPUT select OUTPUT <=
		"1111110" when "0000",
		"0110000" when "0001",
		"1101101" when "0010",
		"1111001" when "0011",
		"0110011" when "0100",
		"1011011" when "0101",
		"1011111" when "0110",
		"1110000" when "0111",
		"1111111" when "1000",
		"1111011" when "1001",
		"1110111" when "1010",
		"0011111" when "1011",
		"1001110" when "1100",
		"0111101" when "1101",
		"1001111" when "1110",
		"1000111" when "1111",
		"0000000" when others;
END Behavioral;

// VHDL entity Debouncer, as the project stores it:
library IEEE;
use IEEE.STD_LOGIC_1164.ALL;
use IEEE.NUMERIC_STD.ALL;

entity Debouncer is
    Port (
        clk    : in  STD_LOGIC;
        button : in  STD_LOGIC;
        debounced_button : out STD_LOGIC
    );
end Debouncer;

architecture Behavioral of Debouncer is
    signal shift_reg : STD_LOGIC_VECTOR(9 downto 0);
    signal debounced_button_reg : STD_LOGIC;
begin
    process (clk)
    begin
        if falling_edge(clk) then
            shift_reg <= shift_reg(8 downto 0) & button;
            if shift_reg = "1111111111" then
            	debounced_button_reg <= '0';
            else 
			debounced_button_reg <= '1';
            end if;
            
        end if;
    end process;

    debounced_button <= debounced_button_reg;
end Behavioral;
