// Logisim project PS2_READER.circ as structural Verilog
module main (
  input  PSCLK,
  input  SYSCLK,
  input  DATA,
  input  RST,
  output Output_1,
  output Output_2,
  output [32:0] Output_bus_1
);

  PS2_READER ps2_reader_1 (
    .CLK(PSCLK), .SYSCLK(SYSCLK), .DATA(DATA), .RESET(RST), .CLICK(Output_1), .N_CLICK(Output_2),
    .TEST(Output_bus_1));
endmodule

// VHDL entity PS2_READER, as the project stores it:
LIBRARY ieee;
USE ieee.std_logic_1164.all;
use ieee.std_logic_unsigned.all;


ENTITY PS2_READER IS
  PORT (
	CLK, SYSCLK, DATA, RESET : in std_logic;
	CLICK, N_CLICK : out std_logic;
	TEST : out std_logic_vector(32 downto 0)
    );
END PS2_READER;

ARCHITECTURE comportm OF PS2_READER IS
	
	COMPONENT SHIFT_REG IS
		PORT(
			CLK, RESET, D : in std_logic;
			Q : out std_logic_vector(32 downto 0)
		);
	END COMPONENT;
	signal TEMPWIRE : std_logic_vector(32 downto 0) := (others => '0');
BEGIN
	SHR : SHIFT_REG port map(CLK, RESET, DATA, TEMPWIRE);
	TEST <= TEMPWIRE;
	process(CLK)
	variable count: std_logic_vector(5 downto 0) := "000000";

	begin
	
	if (falling_edge(CLK)) then
		CLICK <= '0';
		N_CLICK <= '1';
		if (count = "100000") then
			count := "000000";
			if (TEMPWIRE(31) = '0') then
				CLICK <= '1';
				N_CLICK <= '0';
			else 
				CLICK <= '0';
				N_CLICK <= '1';		
			end if;
		else 
			count := count + 1;
		end if;
	end if;

	end process;

END comportm;






LIBRARY ieee;
USE ieee.std_logic_1164.all;
USE ieee.std_logic_unsigned.all;

ENTITY BIST_D IS
  PORT (
	CLK: in std_logic;
	D, S, R: in std_logic;
	Q: out std_logic
    );
END BIST_D;


ARCHITECTURE compr OF BIST_D IS

BEGIN
	process(CLK)
	begin
		if rising_edge(CLK) then
			if (S = '0') then
				Q <= '1';
			elsif (R = '0') then
				Q <= '0';
			else 
				Q <= D;
			end if;
		end if;
	end process;

END compr;





LIBRARY ieee;
USE ieee.std_logic_1164.all;
USE ieee.std_logic_unsigned.all;

ENTITY SHIFT_REG IS
	PORT(
		CLK, RESET, D : in std_logic;
		Q : out std_logic_vector(32 downto 0)
	);
END SHIFT_REG;

ARCHITECTURE struct of SHIFT_REG is
	COMPONENT BIST_D IS
	  PORT (
		CLK: in std_logic;
		D, S, R: in std_logic;
		Q: out std_logic
	    );
	END COMPONENT;

	signal W32, W31, W30, W29, W28, W27, W26, W25, W24, W23, W22, W21, W20, W19, W18, W17, W16, W15, W14, W13, W12, W11, W10, W09, W08, W07, W06, W05, W04, W03, W02, W01, W00 : std_logic;
BEGIN
	D33: BIST_D port map(CLK, D, '1',RESET, W32);
	Q(32) <= W32;
	D32: BIST_D port map(CLK, W32, '1',RESET,W31 );
	Q(31) <= W31;
	D31: BIST_D port map(CLK, W31, '1',RESET,W30 );
	Q(30) <= W30;
	D30: BIST_D port map(CLK, W30, '1',RESET,W29 );
	Q(29) <= W29;
	D29: BIST_D port map(CLK, W29, '1',RESET,W28 );
	Q(28) <= W28;
	D28: BIST_D port map(CLK, W28, '1',RESET,W27 );
	Q(27) <= W27;
	D27: BIST_D port map(CLK, W27, '1',RESET,W26 );
	Q(26) <= W26;
	D26: BIST_D port map(CLK, W26, '1',RESET,W25 );
	Q(25) <= W25;
	D25: BIST_D port map(CLK, W25, '1',RESET,W24 );
	Q(24) <= W24;
	D24: BIST_D port map(CLK, W24, '1',RESET,W23 );
	Q(23) <= W23;
	D23: BIST_D port map(CLK, W23, '1',RESET,W22 );
	Q(22) <= W22;
	D22: BIST_D port map(CLK, W22, '1',RESET,W21 );
	Q(21) <= W21;
	D21: BIST_D port map(CLK, W21, '1',RESET,W20 );
	Q(20) <= W20;
	D20: BIST_D port map(CLK, W20, '1',RESET,W19 );
	Q(19) <= W19;
	D19: BIST_D port map(CLK, W19, '1',RESET,W18 );
	Q(18) <= W18;
	D18: BIST_D port map(CLK, W18, '1',RESET,W17 );
	Q(17) <= W17;
	D17: BIST_D port map(CLK, W17, '1',RESET,W16 );
	Q(16) <= W16;
	D16: BIST_D port map(CLK, W16, '1',RESET,W15 );
	Q(15) <= W15;
	D15: BIST_D port map(CLK, W15, '1',RESET,W14 );
	Q(14) <= W14;
	D14: BIST_D port map(CLK, W14, '1',RESET,W13 );
	Q(13) <= W13;
	D13: BIST_D port map(CLK, W13, '1',RESET,W12 );
	Q(12) <= W12;
	D12: BIST_D port map(CLK, W12, '1',RESET,W11 );
	Q(11) <= W11;
	D11: BIST_D port map(CLK, W11, '1',RESET,W10 );
	Q(10) <= W10;
	D10: BIST_D port map(CLK, W10, '1',RESET,W09 );
	Q(9) <= W09;
	D09: BIST_D port map(CLK, W09, '1',RESET,W08 );
	Q(8) <= W08;
	D08: BIST_D port map(CLK, W08, '1',RESET,W07 );
	Q(7) <= W07;
	D07: BIST_D port map(CLK, W07, '1',RESET,W06 );
	Q(6) <= W06;
	D06: BIST_D port map(CLK, W06, '1',RESET,W05 );
	Q(5) <= W05;
	D05: BIST_D port map(CLK, W05, '1',RESET,W04 );
	Q(4) <= W04;
	D04: BIST_D port map(CLK, W04, '1',RESET,W03 );
	Q(3) <= W03;
	D03: BIST_D port map(CLK, W03, '1',RESET,W02 );
	Q(2) <= W02;
	D02: BIST_D port map(CLK, W02, '1',RESET,W01 );
	Q(1) <= W01;
	D01: BIST_D port map(CLK, W01, '1',RESET,W00);
	Q(0) <= W00;

END struct;
