// Logisim project PS2_READER2.circ as structural Verilog
module main (
  input  Input_1,
  input  Input_2,
  input  Input_3,
  input  Input_4,
  output Output_1,
  output Output_2,
  output [15:0] Output_bus_1
);

  ps2_decoder ps2_decoder_1 (
    .CLOCK(Input_1), .RESET(Input_2), .PS2_CLOCK(Input_3), .PS2_DATA(Input_4), .LEFT_CLICK(Output_1),
    .RIGHT_CLICK(Output_2), .TEST(Output_bus_1));
endmodule

// VHDL entity ps2_decoder, as the project stores it:
-- debouncer useless
LIBRARY ieee;
USE ieee.std_logic_1164.all;
USE ieee.std_logic_unsigned.all;

ENTITY ps2_decoder IS
  PORT (
  	CLOCK: in std_logic;
  	RESET: in std_logic;
  	PS2_CLOCK : in std_logic;
  	PS2_DATA: in std_logic;
  	LEFT_CLICK: inout std_logic;
  	RIGHT_CLICK: inout std_logic;
  	TEST: out std_logic_vector(15 downto 0)
	);
END ps2_decoder;


ARCHITECTURE Behavioral OF ps2_decoder IS

signal MOUSE_REGISTER: std_logic_vector(42 downto 0) := (others => '0');
signal CLICK_COUNT: std_logic_vector(15 downto 0) := (others => '0');
signal MOUSE_BITS: std_logic_vector(5 downto 0) := (others => '0');
signal REGISTER_FULL: std_logic;
signal IS_LEFT_PRESSED: std_logic := '0';
signal IS_RIGHT_PRESSED: std_logic := '0';


BEGIN
    BIT_COUNT_PROCESS: PROCESS(PS2_CLOCK, RESET)
    BEGIN
        IF RESET = '0' then
            MOUSE_BITS <= (others => '0');
        elsif rising_edge(PS2_CLOCK) then
            if MOUSE_BITS <= 42 then
                MOUSE_BITS <= MOUSE_BITS + 1;
            else
                MOUSE_BITS <= (others => '0');
            end if;
        end if;
    END PROCESS;

    REGISTER_PROCESS: PROCESS(PS2_CLOCK, RESET)
    BEGIN
    	   REGISTER_FULL <= '0';
        if RESET = '0' then
            MOUSE_REGISTER <= (others => '0');
        elsif falling_edge(PS2_CLOCK) then
            MOUSE_REGISTER <= MOUSE_REGISTER(41 downto 0) & PS2_DATA;
            if MOUSE_BITS = 42 then
            	REGISTER_FULL <= '1';
            end if;

        end if;
    END PROCESS;	
    	
    COUNTER_PROCESS: PROCESS(CLOCK, RESET)
    BEGIN
        if RESET = '0' then
            CLICK_COUNT <= (others => '0');
        elsif rising_edge(CLOCK) then
        	  if REGISTER_FULL = '1' then
			if MOUSE_REGISTER(41) = '1' and IS_LEFT_PRESSED = '0' then
				CLICK_COUNT <= CLICK_COUNT + 1;
			elsif MOUSE_REGISTER(40) = '1' and IS_RIGHT_PRESSED = '0' then
				CLICK_COUNT <= CLICK_COUNT - 1;
			end if;
			IS_LEFT_PRESSED <= MOUSE_REGISTER(41);
        		IS_RIGHT_PRESSED <= MOUSE_REGISTER(40);
        	  end if;
        end if;
        
        TEST <= CLICK_COUNT;
    END PROCESS;

    
    

END Behavioral;
