// Logisim project mouse_test.circ as structural Verilog
module main (
  input  clk,
  input  RESET,
  input  psclk,
  input  PSDATA,
  output x,
  output [15:0] Output_bus_1
);

  ps2_mse ps2_mse_1 (.CLK(clk), .RST(RESET), .PS2CLK(psclk), .PS2DATA(PSDATA), .LCLICK(x), .TEST(Output_bus_1));
endmodule

// VHDL entity ps2_mse, as the project stores it:
LIBRARY ieee;
USE ieee.std_logic_1164.all;
USE ieee.std_logic_unsigned.all;

ENTITY ps2_mse IS
  PORT (
	CLK, RST, PS2CLK, PS2DATA: in std_logic;
	LCLICK: out std_logic;
	TEST: out std_logic_vector(15 downto 0)
);
END ps2_mse;


ARCHITECTURE comportm OF ps2_mse IS
signal MOUSE_BITS: natural := 0;
signal MOUSE_REG: std_logic_vector(42 downto 0) := (others => '0');
signal TRIGGER : std_logic;

BEGIN
	process(RST, PS2CLK)
	begin
		if RST = '1' then
			MOUSE_BITS <= 0;
		elsif rising_edge(PS2CLK) then
			if MOUSE_BITS <= 42 then
				MOUSE_BITS <= MOUSE_BITS + 1;
			else
				MOUSE_BITS <= 0;
			end if;	
		end if;
	end process;
	
	process(PS2CLK, RST)
	begin
		if RST = '1' then
			MOUSE_REG <= (others => '0');
		elsif falling_edge(PS2CLK) then
			TRIGGER <= '0';
			MOUSE_REG <= MOUSE_REG(41 downto 0) & PS2DATA;
			if MOUSE_BITS = 42 then
			    TRIGGER <= '1';
			end if;
		end if;
	end process;

	process(RST, CLK)
	variable IDLE: boolean := true;
	begin
		if RST = '1' then
			IDLE := true;
		elsif rising_edge(CLK) then
			LCLICK <= '0';
			if TRIGGER = '1' then
				if MOUSE_REG(41) = '1' then
					LCLICK <= '1';
				end if;
				--TEST <= MOUSE_REG(42 downto 27);
			end if;


		end if;
	end process;

END comportm;
