// Logisim project ssd_mgmnt.circ as structural Verilog
module main (
  input  CLK,
  input  RST,
  input  [15:0] INPT,
  output CLK_OUT,
  output [3:0] ANODE,
  output [6:0] SSD
);

  wire ssd_controller_1_reset_decd;
  wire [1:0] ssd_controller_1_anode;

  divizor_f divizor_f_1 (.CLK_100(CLK), .RST(1'b1), .CLK_1(CLK_OUT));
  ssd_controller ssd_controller_1 (
    .REDUCED_CLK(CLK_OUT), .RESET(RST), .ANODE(ssd_controller_1_anode),
    .RESET_DECD(ssd_controller_1_reset_decd));
  ssd_decd ssd_decd_1 (
    .CLK(CLK_OUT), .RESET(ssd_controller_1_reset_decd), .ANODE_IN(ssd_controller_1_anode), .NR(INPT),
    .ANODE_OUT(ANODE), .SSD_OUT(SSD));
endmodule

// VHDL entity ssd_controller, as the project stores it:
--------------------------------------------------------------------------------
-- Project :
-- File    :
-- Autor   :
-- Date    :
--
--------------------------------------------------------------------------------
-- Description :
--
--------------------------------------------------------------------------------

LIBRARY ieee;
USE ieee.std_logic_1164.all;
USE ieee.std_logic_unsigned.all;

ENTITY ssd_controller IS
  PORT (
	REDUCED_CLK, RESET: in std_logic;
	ANODE: out std_logic_vector(1 downto 0);
	RESET_DECD: out std_logic
    );
END ssd_controller;

--------------------------------------------------------------------------------
--Complete your VHDL description below
--------------------------------------------------------------------------------

ARCHITECTURE comprtm OF ssd_controller IS
type STARE_T is (D0, D1, D2, D3);
signal STARE, NXSTARE : STARE_T;
BEGIN
	CTRL: process(REDUCED_CLK, RESET)
	begin
		if RESET = '1' then
			RESET_DECD <= '1';
			STARE <= D0;
		elsif rising_edge(REDUCED_CLK) then
			STARE <= NXSTARE;
			RESET_DECD <= '0';
		end if;
		
	end process CTRL;

	TRANZ: process(STARE)
	
	begin
		ANODE <= "00";
		case STARE is
			when D0 => ANODE <= "00"; NXSTARE <= D1;
			when D1 => ANODE <= "01"; NXSTARE <= D2;
			when D2 => ANODE <= "10"; NXSTARE <= D3;
			when D3 => ANODE <= "11"; NXSTARE <= D0;
		end case;
	end process TRANZ;
	

END comprtm;

// VHDL entity ssd_decd, as the project stores it:
--------------------------------------------------------------------------------
-- Project :
-- File    :
-- Autor   :
-- Date    :
--
--------------------------------------------------------------------------------
-- Description :
--
--------------------------------------------------------------------------------

LIBRARY ieee;
USE ieee.std_logic_1164.all;
use ieee.std_logic_unsigned.all;
use ieee.numeric_std.all;

ENTITY ssd_decd IS
  PORT (
  	CLK, RESET: in std_logic;
	ANODE_IN :in std_logic_vector(1 downto 0);
	NR: in std_logic_vector(15 downto 0);
	ANODE_OUT : out std_logic_vector(3 downto 0);
	SSD_OUT: out std_logic_vector(6 downto 0)
    );
END ssd_decd;

--------------------------------------------------------------------------------
--Complete your VHDL description below
--------------------------------------------------------------------------------

ARCHITECTURE comportm OF ssd_decd IS
signal BIN_NR : std_logic_vector(3 downto 0);
BEGIN
	process(CLK, RESET)
	variable temp: integer;
	begin
--		BIN_NR <= "0000";
--		ANODE_OUT <= "0000";
		if RESET = '1' then		
			ANODE_OUT <= "0000";
			SSD_OUT <= "0000000";
		elsif rising_edge(CLK) then
			--Afisarea se face in hexa dar se poate modifica in zecimal daca trec la integer si tot iau ultima cifra
--			case ANODE_IN is
--				when "00" => BIN_NR <= NR(3 downto 0); ANODE_OUT <= "0001";
--				when "01" => BIN_NR <= NR(7 downto 4); ANODE_OUT <= "0010";
--				when "10" => BIN_NR <= NR(11 downto 8); ANODE_OUT <= "0100";
--				when "11" => BIN_NR <= NR(15 downto 12); ANODE_OUT <= "1000";
--				when others => ANODE_OUT <= "0000";
--			end case;
			temp := conv_integer(NR);
			case ANODE_IN is
				when "00" => BIN_NR <= std_logic_vector(to_unsigned(temp rem 10, BIN_NR'length)); ANODE_OUT <= "0001";
				when "01" => BIN_NR <= std_logic_vector(to_unsigned((temp / 10 ) rem 10, BIN_NR'length)); ANODE_OUT <= "0010";
				when "10" => BIN_NR <= std_logic_vector(to_unsigned((temp / 100) rem 10, BIN_NR'length)); ANODE_OUT <= "0100";
				when "11" => BIN_NR <= std_logic_vector(to_unsigned((temp / 1000) rem 10, BIN_NR'length)); ANODE_OUT <= "1000";
				when others => ANODE_OUT <= "0000";
			end case;
			
			SSD_OUT <= "0000000";
			case BIN_NR is
				when "0000" => SSD_OUT <= "1111110";
				when "0001" => SSD_OUT <= "0110000";
				when "0010" => SSD_OUT <= "1101101";
				when "0011" => SSD_OUT <= "1111001";
				when "0100" => SSD_OUT <= "0110011";
				when "0101" => SSD_OUT <= "1011011";
				when "0110" => SSD_OUT <= "0011111";
				when "0111" => SSD_OUT <= "1110000";
				when "1000" => SSD_OUT <= "1111111";
				when "1001" => SSD_OUT <= "1110011";
				when "1010" => SSD_OUT <= "1110111";
				when "1011" => SSD_OUT <= "0011111";
				when "1100" => SSD_OUT <= "1001110";
				when "1101" => SSD_OUT <= "0111101";
				when "1110" => SSD_OUT <= "1001111";
				when "1111" => SSD_OUT <= "1000111";
				when others => SSD_OUT <= "0000000";
			end case;
		end if;
	end process;

END comportm;

// VHDL entity divizor_f, as the project stores it:
LIBRARY ieee;
USE ieee.std_logic_1164.all;
USE ieee.std_logic_unsigned.all;

ENTITY divizor_f IS
  PORT (
  	CLK_100: in std_logic;
  	RST: in std_logic;
  	CLK_1: out std_logic
	);
END divizor_f;


ARCHITECTURE comportm OF divizor_f IS

BEGIN

	process(CLK_100)
	variable nr: std_logic_vector (10 downto 0) := (others => '0');
	begin
		if rising_edge(CLK_100) then
			if RST = '0' then
				nr := (others => '0');
			else
				nr := nr + 1;
			end if;
		end if;
		CLK_1 <= nr(10);
	end process;

END comportm;

// VHDL entity bistabil_d, as the project stores it:
LIBRARY ieee;
USE ieee.std_logic_1164.all;
USE ieee.std_logic_unsigned.all;

ENTITY bistabil_d IS
  PORT (
	CLK: in std_logic;
	D, S, R: in std_logic;
	Q: out std_logic
    );
END bistabil_d;


ARCHITECTURE compr OF bistabil_d IS

BEGIN

	process(CLK)
	begin
		if rising_edge(CLK) then
			if (S = '0') then
				Q <= '1';
			elsif (R = '0') then
				Q <= '0';
			else 
				Q <= D;
			end if;
		end if;
	end process;

END compr;
